// Logisim project Lab1_computadores.circ as structural Verilog: 7 circuits, main circuit main
module main (
  input  in_1,
  input  in_2,
  input  in_3,
  output out_4,
  output out_5
);

  Sumador sumador_1 (.A(in_2), .B(in_3), .Cin(in_1), .S(out_4), .Cout(out_5));
  Sumador_overflow sumador_overflow_1 ();  // open: A, B, Cin, S, Cout, Overflow
endmodule

module Sumador (
  input  A,
  input  B,
  input  Cin,
  output S,
  output Cout
);

  wire and_1_out, and_2_out, and_3_out, and_4_out, and_5_out, and_6_out, and_7_out, not_1_out, not_2_out,
       not_3_out, not_4_out, not_5_out, not_6_out;

  not not_1 (not_1_out, A);
  not not_2 (not_2_out, B);
  not not_3 (not_3_out, A);
  not not_4 (not_4_out, Cin);
  not not_5 (not_5_out, B);
  not not_6 (not_6_out, Cin);
  and and_1 (and_1_out, B, Cin);
  and and_2 (and_2_out, A, Cin);
  and and_3 (and_3_out, A, B);
  and and_4 (and_4_out, not_1_out, not_2_out, Cin);
  and and_5 (and_5_out, not_3_out, B, not_4_out);
  and and_6 (and_6_out, A, not_5_out, not_6_out);
  and and_7 (and_7_out, A, B, Cin);
  or or_1 (Cout, and_1_out, and_2_out, and_3_out);
  or or_2 (S, and_4_out, and_5_out, and_6_out, and_7_out);
endmodule

module Sumador_overflow (
  input  A,
  input  B,
  input  Cin,
  output S,
  output Cout,
  output Overflow
);

  wire and_1_out, and_2_out, and_3_out, and_4_out, and_5_out, and_6_out, and_7_out, and_8_out, and_9_out,
       not_1_out, not_2_out, not_3_out, not_4_out, not_5_out, not_6_out, not_7_out;

  not not_1 (not_1_out, A);
  not not_2 (not_2_out, B);
  not not_3 (not_3_out, A);
  not not_4 (not_4_out, Cin);
  not not_5 (not_5_out, B);
  not not_6 (not_6_out, Cin);
  and and_1 (and_1_out, B, Cin);
  and and_2 (and_2_out, A, Cin);
  and and_3 (and_3_out, A, B);
  and and_4 (and_4_out, not_1_out, not_2_out, Cin);
  and and_5 (and_5_out, not_3_out, B, not_4_out);
  and and_6 (and_6_out, A, not_5_out, not_6_out);
  and and_7 (and_7_out, A, B, Cin);
  or or_1 (Cout, and_1_out, and_2_out, and_3_out);
  not not_7 (not_7_out, Cout);
  or or_2 (S, and_4_out, and_5_out, and_6_out, and_7_out);
  and and_8 (and_8_out, not_7_out, Cin);
  and and_9 (and_9_out, not_6_out, Cout);
  or or_3 (Overflow, and_8_out, and_9_out);
endmodule

module ALU_bit_1 (
  input  A,
  input  B,
  input  Cint,
  input  SLT,
  input  Binvert,
  input  [2:0] Op,
  output R,
  output Cout
);

  wire and_1_out, multiplexer_1_out, not_1_out, not_2_out, or_1_out, sumador_1_s;

  not not_1 (not_1_out, B);
  Multiplexer multiplexer_1 (.in0(B), .in1(not_1_out), .out(multiplexer_1_out), .sel(Binvert));  // open: en
  and and_1 (and_1_out, B, A);
  or or_1 (or_1_out, B, A);
  not not_2 (not_2_out, or_1_out);
  Sumador sumador_1 (.A(A), .B(multiplexer_1_out), .Cin(Cint), .S(sumador_1_s), .Cout(Cout));
  Multiplexer #(.select(3), .enable("false")) multiplexer_2 (
    .in0(and_1_out), .in1(sumador_1_s), .in3(sumador_1_s), .in4(not_2_out), .in6(or_1_out), .in7(SLT),
    .out(R), .sel(Op));  // open: in2, in5
endmodule

// A12
module ALU_bit_16 (
  input  [15:0] in_1,
  input  [2:0] in_2,
  input  [15:0] in_3,
  input  [3:0] in_4,
  output [15:0] out_5,
  output out_6,
  output out_7
);

  wire alu_bit_1_1_cout, alu_bit_1_2_cout, alu_bit_1_3_cout, alu_bit_1_4_cout, alu_bit_1_5_cout,
       alu_bit_1_6_cout, alu_bit_1_7_cout, alu_bit_1_8_cout, alu_bit_1_9_cout, alu_bit_1_10_cout,
       alu_bit_1_11_cout, alu_bit_1_12_cout, alu_bit_1_13_cout, alu_bit_1_14_cout, alu_bit_1_15_cout,
       and_1_out, and_2_out, or_1_out, slt;
  wire [15:0] decoder_1_out0;

  and and_1 (and_1_out, in_2[2], in_2[1], in_2[0]);
  and and_2 (and_2_out, ~in_2[2], ~in_2[1], in_2[0]);  // AND_Gate
  // Probe on in_1
  or or_1 (or_1_out, and_2_out, and_1_out);
  // Probe on in_3
  Decoder_part #(.select(4)) decoder_1 (
    .out0(decoder_1_out0[0]), .out1(decoder_1_out0[1]), .out2(decoder_1_out0[2]), .out3(decoder_1_out0[3]),
    .out4(decoder_1_out0[4]), .out5(decoder_1_out0[5]), .out6(decoder_1_out0[6]), .out7(decoder_1_out0[7]),
    .out8(decoder_1_out0[8]), .out9(decoder_1_out0[9]), .out10(decoder_1_out0[10]),
    .out11(decoder_1_out0[11]), .out12(decoder_1_out0[12]), .out13(decoder_1_out0[13]),
    .out14(decoder_1_out0[14]), .out15(decoder_1_out0[15]), .sel(in_4));  // open: en
  ALU_bit_1 alu_bit_1_1 (
    .R(out_5[0]), .A(in_1[0]), .B(in_3[0]), .Cint(or_1_out), .Op(in_2), .Cout(alu_bit_1_1_cout),
    .Binvert(or_1_out), .SLT(slt));
  ALU_bit_1 alu_bit_1_2 (
    .R(out_5[1]), .A(in_1[1]), .B(in_3[1]), .Cint(alu_bit_1_1_cout), .Op(in_2), .Cout(alu_bit_1_2_cout),
    .Binvert(or_1_out), .SLT(1'b0));
  ALU_bit_1 alu_bit_1_3 (
    .R(out_5[2]), .A(in_1[2]), .B(in_3[2]), .Cint(alu_bit_1_2_cout), .Op(in_2), .Cout(alu_bit_1_3_cout),
    .Binvert(or_1_out), .SLT(1'b0));
  ALU_bit_1 alu_bit_1_4 (
    .R(out_5[3]), .A(in_1[3]), .B(in_3[3]), .Cint(alu_bit_1_3_cout), .Op(in_2), .Cout(alu_bit_1_4_cout),
    .Binvert(or_1_out), .SLT(1'b0));
  ALU_bit_1 alu_bit_1_5 (
    .R(out_5[4]), .A(in_1[4]), .B(in_3[4]), .Cint(alu_bit_1_4_cout), .Op(in_2), .Cout(alu_bit_1_5_cout),
    .Binvert(or_1_out), .SLT(1'b0));
  ALU_bit_1 alu_bit_1_6 (
    .R(out_5[5]), .A(in_1[5]), .B(in_3[5]), .Cint(alu_bit_1_5_cout), .Op(in_2), .Cout(alu_bit_1_6_cout),
    .Binvert(or_1_out), .SLT(1'b0));
  ALU_bit_1 alu_bit_1_7 (
    .R(out_5[6]), .A(in_1[6]), .B(in_3[6]), .Cint(alu_bit_1_6_cout), .Op(in_2), .Cout(alu_bit_1_7_cout),
    .Binvert(or_1_out), .SLT(1'b0));
  ALU_bit_1 alu_bit_1_8 (
    .R(out_5[7]), .A(in_1[7]), .B(in_3[7]), .Cint(alu_bit_1_7_cout), .Op(in_2), .Cout(alu_bit_1_8_cout),
    .Binvert(or_1_out), .SLT(1'b0));
  // Probe on decoder_1_out0
  ALU_bit_1 alu_bit_1_9 (
    .R(out_5[8]), .A(in_1[8]), .B(in_3[8]), .Cint(alu_bit_1_8_cout), .Op(in_2), .Cout(alu_bit_1_9_cout),
    .Binvert(or_1_out), .SLT(1'b0));
  ALU_bit_1 alu_bit_1_10 (
    .R(out_5[9]), .A(in_1[9]), .B(in_3[9]), .Cint(alu_bit_1_9_cout), .Op(in_2), .Cout(alu_bit_1_10_cout),
    .Binvert(or_1_out), .SLT(1'b0));
  ALU_bit_1 alu_bit_1_11 (
    .R(out_5[10]), .A(in_1[10]), .B(in_3[10]), .Cint(alu_bit_1_10_cout), .Op(in_2), .Cout(alu_bit_1_11_cout),
    .Binvert(or_1_out), .SLT(1'b0));
  ALU_bit_1 alu_bit_1_12 (
    .R(out_5[11]), .A(in_1[11]), .B(in_3[11]), .Cint(alu_bit_1_11_cout), .Op(in_2), .Cout(alu_bit_1_12_cout),
    .Binvert(or_1_out), .SLT(1'b0));
  ALU_bit_1 alu_bit_1_13 (
    .R(out_5[12]), .A(in_1[12]), .B(in_3[12]), .Cint(alu_bit_1_12_cout), .Op(in_2), .Cout(alu_bit_1_13_cout),
    .Binvert(or_1_out), .SLT(1'b0));
  ALU_bit_1 alu_bit_1_14 (
    .R(out_5[13]), .A(in_1[13]), .B(in_3[13]), .Cint(alu_bit_1_13_cout), .Op(in_2), .Cout(alu_bit_1_14_cout),
    .Binvert(or_1_out), .SLT(1'b0));
  ALU_bit_1 alu_bit_1_15 (
    .R(out_5[14]), .A(in_1[14]), .B(in_3[14]), .Cint(alu_bit_1_14_cout), .Op(in_2), .Cout(alu_bit_1_15_cout),
    .Binvert(or_1_out), .SLT(1'b0));
  // Probe on alu_bit_1_15_cout
  ALU_BIT_1_overflow alu_bit_1_overflow_1 (
    .A(in_1[15]), .B(in_3[15]), .Cint(alu_bit_1_15_cout), .R(out_5[15]), .overFlow(out_6), .Cout(out_7),
    .Op(in_2), .Binvert(or_1_out), .SLT(1'b0), .slt_2(slt));
  // Probe on out_5

  // Other names for the same wires on the sheet: A0 = in_1[0]; A1 = in_1[1]; A2 = in_1[2]; A3 = in_1[3]; A4 = in_1[4];
  //   A5 = in_1[5]; A6 = in_1[6]; A7 = in_1[7]; A8 = in_1[8]; A9 = in_1[9]; A10 = in_1[10]; A11 = in_1[11];
  //   A12 = in_1[12]; A13 = in_1[13]; A14 = in_1[14]; A15 = in_1[15]; B0 = in_3[0]; B1 = in_3[1]; B2 = in_3[2];
  //   B3 = in_3[3]; B4 = in_3[4]; B5 = in_3[5]; B6 = in_3[6]; B7 = in_3[7]; B8 = in_3[8]; B9 = in_3[9];
  //   B10 = in_3[10]; B11 = in_3[11]; B12 = in_3[12]; B13 = in_3[13]; B14 = in_3[14]; B15 = in_3[15]; OP[2:0] = in_2;
  //   R0 = out_5[0]; R1 = out_5[1]; R2 = out_5[2]; R3 = out_5[3]; R4 = out_5[4]; R5 = out_5[5]; R6 = out_5[6];
  //   R7 = out_5[7]; R8 = out_5[8]; R9 = out_5[9]; R10 = out_5[10]; R11 = out_5[11]; R12 = out_5[12]; R13 = out_5[13];
  //   R14 = out_5[14]; R15 = out_5[15]

  // Notes on the sheet:
  //   Binvert
endmodule

module ALU_BIT_1_overflow (
  input  A,
  input  B,
  input  Cint,
  input  SLT,
  input  Binvert,
  input  [2:0] Op,
  output R,
  output slt_2,
  output overFlow,
  output Cout
);

  wire and_1_out, multiplexer_1_out, not_1_out, not_2_out, or_1_out, or_2_out;

  not not_1 (not_1_out, B);
  Multiplexer multiplexer_1 (.in0(B), .in1(not_1_out), .out(multiplexer_1_out), .sel(Binvert));  // open: en
  and and_1 (and_1_out, B, A);
  or or_1 (or_1_out, B, A);
  not not_2 (not_2_out, or_2_out);
  or or_2 (or_2_out, B, A);
  Sumador_overflow sumador_overflow_1 (
    .A(multiplexer_1_out), .B(A), .Cin(Cint), .S(slt_2), .Cout(Cout), .Overflow(overFlow));
  Multiplexer #(.select(3), .enable("false")) multiplexer_2 (
    .in0(and_1_out), .in1(slt_2), .in3(slt_2), .in4(not_2_out), .in6(or_1_out), .in7(SLT), .out(R), .sel(Op));  // open: in2, in5
endmodule

module Decoder (
  input  [3:0] in_1
);

  wire and_1_out;

  and and_1 (and_1_out, ~in_1[3], ~in_1[2], ~in_1[1], ~in_1[0]);  // AND_Gate

  // Other names for the same wires on the sheet: D = in_1[0]; C = in_1[1]; B = in_1[2]; A = in_1[3]
endmodule
