// Logisim project Lab2_computadores.circ as structural Verilog: 7 circuits, main circuit main
module main (
  input  in_1,
  input  in_2,
  input  in_3
);

  wire reconocedor_sec_1_s1, reconocedor_sec_1_s2, reconocedor_sec_1_s3, reconocedor_sec_1_s4;
  wire [3:0] reconocedor_sec_1_out_4;

  Reconocedor_sec reconocedor_sec_1 (
    .in_1(in_1), .Reset(in_3), .out_4(reconocedor_sec_1_out_4), .S1(reconocedor_sec_1_s1),
    .S2(reconocedor_sec_1_s2), .S3(reconocedor_sec_1_s3), .S4(reconocedor_sec_1_s4), .Clk(in_2));
  LED S4 (.in(reconocedor_sec_1_s4));
  LED S3 (.in(reconocedor_sec_1_s3));
  LED S2 (.in(reconocedor_sec_1_s2));
  LED S1 (.in(reconocedor_sec_1_s1));
endmodule

module Reconocedor_sec (
  input  in_1,
  input  Reset,
  input  Clk,
  output [3:0] out_4,
  output S1,
  output S2,
  output S3,
  output S4
);

  wire J1, J2, J3, J4, K1, K2, K3, K4;

  J4K4 j4k4_1 (.A(out_4[0]), .B(out_4[1]), .C(out_4[2]), .E(in_1), .J4(J4), .K4(K4));
  J1K1 j1k1_1 (.B(out_4[1]), .C(out_4[2]), .E(in_1), .D(out_4[3]), .J1(J1), .K1(K1));
  J2K2 j2k2_1 (.A(out_4[0]), .C(out_4[2]), .D(out_4[3]), .E(in_1), .J2(J2), .K2(K2));
  J3K3 j3k3_1 (.A(out_4[0]), .B(out_4[1]), .D(out_4[3]), .E(in_1), .J3(J3), .K3(K3));
  Y1Y2Y3Y4 y1y2y3y4_1 (.A(out_4[0]), .B(out_4[1]), .C(out_4[2]), .D(out_4[3]), .Y1(S1), .Y2(S2), .Y3(S3), .Y4(S4));
  J_K_Flip_Flop j_k_ff_1 (.J(J4), .clk(Clk), .K(K4), .Q(out_4[3]), .reset(Reset));  // open: Qn, preset, en
  J_K_Flip_Flop j_k_ff_2 (.J(J3), .clk(Clk), .K(K3), .Q(out_4[2]), .reset(Reset));  // open: Qn, preset, en
  J_K_Flip_Flop j_k_ff_3 (.J(J2), .clk(Clk), .K(K2), .Q(out_4[1]), .reset(Reset));  // open: Qn, preset, en
  J_K_Flip_Flop j_k_ff_4 (.J(J1), .clk(Clk), .K(K1), .Q(out_4[0]), .reset(Reset));  // open: Qn, preset, en

  // Other names for the same wires on the sheet: Q1 = out_4[0]; Q2 = out_4[1]; Q3 = out_4[2]; Q4 = out_4[3]; X = in_1;
  //   Y1 = S1; Y2 = S2; Y3 = S3; Y4 = S4
endmodule

module J2K2 (
  input  A,
  input  C,
  input  D,
  input  E,
  output J2,
  output K2
);

  wire and_1_out, and_2_out, and_3_out, and_4_out, and_5_out, and_6_out, and_7_out;

  and and_1 (and_1_out, ~A, C);  // AND_Gate
  and and_2 (and_2_out, A, E);
  and and_3 (and_3_out, A, ~C, D);  // AND_Gate
  and and_4 (and_4_out, ~D, ~E);  // AND_Gate
  and and_5 (and_5_out, C, E);
  and and_6 (and_6_out, ~A, ~C, ~E);  // AND_Gate
  and and_7 (and_7_out, A, D, E);
  or or_1 (J2, and_1_out, and_2_out, and_3_out);
  or or_2 (K2, and_4_out, and_5_out, and_6_out, and_7_out);
endmodule

module J3K3 (
  input  A,
  input  B,
  input  D,
  input  E,
  output J3,
  output K3
);

  wire and_1_out, and_2_out, and_3_out, and_4_out, and_5_out;

  and and_1 (and_1_out, ~B, E);  // AND_Gate
  and and_2 (and_2_out, ~A, ~B, E);  // AND_Gate
  and and_3 (and_3_out, ~A, ~D, E);  // AND_Gate
  and and_4 (and_4_out, A, ~B, ~D);  // AND_Gate
  and and_5 (and_5_out, A, D, ~E);  // AND_Gate
  or or_1 (J3, and_2_out, and_3_out, and_4_out, and_5_out);
  or or_2 (K3, ~D, A, and_1_out);  // OR_Gate
endmodule

module J4K4 (
  input  A,
  input  B,
  input  C,
  input  E,
  output J4,
  output K4
);

  wire and_1_out, and_2_out, and_3_out, and_4_out, and_5_out, and_6_out, and_7_out, and_8_out, and_9_out;

  and and_1 (and_1_out, C, E);
  and and_2 (and_2_out, ~A, B);  // AND_Gate
  and and_3 (and_3_out, B, C);
  and and_4 (and_4_out, A, E);
  and and_5 (and_5_out, ~B, ~C, ~E);  // AND_Gate
  or or_1 (J4, and_1_out, and_2_out, and_3_out, and_4_out, and_5_out);
  and and_6 (and_6_out, B, ~E);  // AND_Gate
  and and_7 (and_7_out, B, C);
  and and_8 (and_8_out, ~A, C, ~E);  // AND_Gate
  and and_9 (and_9_out, A, ~B, ~C);  // AND_Gate
  or or_2 (K4, and_6_out, and_7_out, and_8_out, and_9_out);
endmodule

module Y1Y2Y3Y4 (
  input  A,
  input  B,
  input  C,
  input  D,
  output Y1,
  output Y2,
  output Y3,
  output Y4
);

  wire and_2_out, and_3_out;

  and and_1 (Y1, A, ~B, ~C, ~D);  // AND_Gate
  and and_2 (and_2_out, A, ~B, C, ~D);  // AND_Gate
  and and_3 (and_3_out, A, B, ~C, ~D);  // AND_Gate
  and and_4 (Y3, A, B, ~C, ~D);  // AND_Gate
  and and_5 (Y4, A, B, C, ~D);  // AND_Gate
  or or_1 (Y2, and_2_out, and_3_out);
endmodule

module J1K1 (
  input  B,
  input  C,
  input  E,
  input  D,
  output J1,
  output K1
);

  wire and_1_out, and_2_out, and_3_out, and_4_out, and_5_out, and_6_out;

  and and_1 (and_1_out, B, C, E);
  and and_2 (and_2_out, B, ~C, D, ~E);  // AND_Gate
  and and_3 (and_3_out, ~B, ~D, E);  // AND_Gate
  and and_4 (and_4_out, ~B, D, ~E);  // AND_Gate
  and and_5 (and_5_out, B, ~C, E);  // AND_Gate
  and and_6 (and_6_out, B, C, ~E);  // AND_Gate
  or or_1 (J1, and_1_out, and_2_out);
  or or_2 (K1, and_3_out, and_4_out, and_5_out, and_6_out);
endmodule
